# Fritzing sketch FinalSketch (saved by Fritzing 0.9.3b)
breadboards: 1

parts:
  NodeMCU = NodeMCU V1.0
  L298N_Motor_Driver = L298N DC motor driver
  IR_Sensor = fc-51 [package=THT]
  Pushing_Piston = DC Motor
  Conveyor_Belt = DC Motor
  DC_Socket = 2.1mm Barrel Jack with Terminal Block

nets:
  N1: NodeMCU.D2, IR_Sensor.pin1
  N2: NodeMCU.GND, IR_Sensor.pin2, DC_Socket.NEG
  N3: NodeMCU.Vin, IR_Sensor.pin3, DC_Socket.POS
  N4: L298N_Motor_Driver.OUT1, Conveyor_Belt.pin_2
  N5: L298N_Motor_Driver.OUT2, Conveyor_Belt.pin_1
  N6: L298N_Motor_Driver.OUT3, Pushing_Piston.pin_2
  N7: L298N_Motor_Driver.OUT4, Pushing_Piston.pin_1
  N8: L298N_Motor_Driver.5V#9, L298N_Motor_Driver.ENA
  N9: L298N_Motor_Driver.5V#10, L298N_Motor_Driver.ENB

custom parts:
  NodeMCU V1.0: ESP8266 based NodeMCU
  L298N DC motor driver: 2x DC motor driver with 78M05 positive voltage regulator (7..35 V) L298N: max 46 V, 2 A Set 5 V Enable jumper to enable 5 V regultor (needed for the L298N) and +5 V output at screw terminal or supply external +5 V at screw terminal Set ENA and/or ENB to +5 V to enable motor permanently or supply ENA and/or ENB with PWM signal IN1 and IN2 set rotation directory for motor A (OUT1/OUT2) IN2 and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
